// Logisim project APS.circ as structural Verilog: 18 circuits, main circuit main
module main (
  input  Reset
);

  wire and_1_out, clock_1_out, controlabola_1_pontobarra1, controlabola_1_pontobarra2, display_1_a,
       display_1_b, display_1_c, display_1_d, display_1_e, display_1_f, display_1_g, display_2_a,
       display_2_b, display_2_c, display_2_d, display_2_e, display_2_f, display_2_g, not_1_out, or_1_out,
       or_2_out, placar_1_acabou_venceu, placar_2_acabou_venceu;
  wire [2:0] placar_1_pontosmarcados, placar_2_pontosmarcados;
  wire [3:0] controlabola_1_out_horizontal, controlabola_1_out_vertical, ia_1_posicao_barra,
       pegateclado_1_out__4bits;
  wire [6:0] keyboard_1_data;
  wire [14:0] controlavisual_1_out_7, controlavisual_1_out_8, controlavisual_1_out_9,
       controlavisual_1_out_10, controlavisual_1_out_11, controlavisual_1_out_12, controlavisual_1_out_13,
       controlavisual_1_out_14, controlavisual_1_out_15, controlavisual_1_out_16, controlavisual_1_out_17,
       controlavisual_1_out_18, controlavisual_1_out_19, controlavisual_1_quinze, controlavisual_1_zero;

  Clock #(.highDuration(2), .lowDuration(2)) clock_1 (.out(clock_1_out));
  and and_1 (and_1_out, clock_1_out, ~or_2_out);  // AND_Gate
  Keyboard keyboard_1 (.clk(and_1_out), .data(keyboard_1_data));  // open: re, clr, avail
  _7_Segment_Display u_7_segment_display_1 (
    .g(display_1_g), .f(display_1_f), .a(display_1_a), .b(display_1_b), .e(display_1_e), .d(display_1_d),
    .c(display_1_c));  // open: dp
  Display display_1 (
    .in_1(placar_2_pontosmarcados), .A(display_1_a), .B(display_1_b), .C(display_1_c), .D(display_1_d),
    .E(display_1_e), .F(display_1_f), .G(display_1_g));
  PegaTeclado pegateclado_1 (
    .In__7bits(keyboard_1_data), .Reset(or_1_out), .Clock(and_1_out), .Out__4bits(pegateclado_1_out__4bits));
  or or_1 (or_1_out, or_2_out, controlabola_1_pontobarra1, controlabola_1_pontobarra2);
  not not_1 (not_1_out, Reset);
  DotMatrix #(.matrixcols(15), .matrixrows(15)) dotmatrix_1 (
    .col0(controlavisual_1_zero), .col1(controlavisual_1_out_7), .col2(controlavisual_1_out_8),
    .col3(controlavisual_1_out_9), .col4(controlavisual_1_out_10), .col5(controlavisual_1_out_11),
    .col6(controlavisual_1_out_12), .col7(controlavisual_1_out_13), .col8(controlavisual_1_out_14),
    .col9(controlavisual_1_out_15), .col10(controlavisual_1_out_16), .col11(controlavisual_1_out_17),
    .col12(controlavisual_1_out_18), .col13(controlavisual_1_out_19), .col14(controlavisual_1_quinze));
  ControlaVisual controlavisual_1 (
    .Acabou(or_2_out), .bum(pegateclado_1_out__4bits), .vertical(controlabola_1_out_vertical),
    .horizontal(controlabola_1_out_horizontal), .bdois(ia_1_posicao_barra), .zero(controlavisual_1_zero),
    .out_7(controlavisual_1_out_7), .out_8(controlavisual_1_out_8), .out_9(controlavisual_1_out_9),
    .out_10(controlavisual_1_out_10), .out_11(controlavisual_1_out_11), .out_12(controlavisual_1_out_12),
    .out_13(controlavisual_1_out_13), .out_14(controlavisual_1_out_14), .out_15(controlavisual_1_out_15),
    .out_16(controlavisual_1_out_16), .out_17(controlavisual_1_out_17), .out_18(controlavisual_1_out_18),
    .out_19(controlavisual_1_out_19), .quinze(controlavisual_1_quinze));
  ControlaBola controlabola_1 (
    .Barra1(pegateclado_1_out__4bits), .Barra2(ia_1_posicao_barra), .Ligar(not_1_out), .Clock(and_1_out),
    .OUT_Horizontal(controlabola_1_out_horizontal), .PontoBarra2(controlabola_1_pontobarra2),
    .PontoBarra1(controlabola_1_pontobarra1), .OUT_Vertical(controlabola_1_out_vertical));
  IA ia_1 (
    .bola_vertical(controlabola_1_out_vertical), .Clock(and_1_out), .inicio(or_1_out),
    .posicao_barra(ia_1_posicao_barra));
  Placar placar_1 (
    .MarcarPonto(controlabola_1_pontobarra2), .Clock(and_1_out), .Reset(Reset),
    .Acabou_Venceu(placar_1_acabou_venceu), .PontosMarcados(placar_1_pontosmarcados));
  Placar placar_2 (
    .MarcarPonto(controlabola_1_pontobarra1), .Clock(and_1_out), .Reset(Reset),
    .Acabou_Venceu(placar_2_acabou_venceu), .PontosMarcados(placar_2_pontosmarcados));
  _7_Segment_Display u_7_segment_display_2 (
    .g(display_2_g), .f(display_2_f), .a(display_2_a), .b(display_2_b), .e(display_2_e), .d(display_2_d),
    .c(display_2_c));  // open: dp
  Display display_2 (
    .in_1(placar_1_pontosmarcados), .A(display_2_a), .B(display_2_b), .C(display_2_c), .D(display_2_d),
    .E(display_2_e), .F(display_2_f), .G(display_2_g));
  or or_2 (or_2_out, placar_1_acabou_venceu, placar_2_acabou_venceu);
endmodule

module ControlaVisual (
  input  Acabou,
  input  [3:0] bum,
  input  [3:0] vertical,
  input  [3:0] horizontal,
  input  [3:0] bdois,
  output [14:0] zero,
  output [14:0] out_7,
  output [14:0] out_8,
  output [14:0] out_9,
  output [14:0] out_10,
  output [14:0] out_11,
  output [14:0] out_12,
  output [14:0] out_13,
  output [14:0] out_14,
  output [14:0] out_15,
  output [14:0] out_16,
  output [14:0] out_17,
  output [14:0] out_18,
  output [14:0] out_19,
  output [14:0] quinze
);

  wire [14:0] adder_1_out, adder_2_out, bin4_bin15_1_out__15bits, bin4_bin15_2_out__15bits,
       bin4_bin15_3_out__15bits, demultiplexer_1_out1, demultiplexer_1_out2, demultiplexer_1_out3,
       demultiplexer_1_out4, demultiplexer_1_out5, demultiplexer_1_out6, demultiplexer_1_out7,
       demultiplexer_1_out8, demultiplexer_1_out9, demultiplexer_1_out10, demultiplexer_1_out11,
       demultiplexer_1_out12, demultiplexer_1_out13, demultiplexer_1_out14, demultiplexer_1_out15,
       monta_barra_1_out__barra_completa, monta_barra_2_out__barra_completa;

  Bin4_bin15 bin4_bin15_1 (.In__4bits(bum), .Out__15bits(bin4_bin15_1_out__15bits));
  Monta_barra monta_barra_1 (
    .In__Posicao_central_de_referencia_da_barra(bin4_bin15_1_out__15bits),
    .Out__barra_completa(monta_barra_1_out__barra_completa));
  Bin4_bin15 bin4_bin15_2 (.In__4bits(vertical), .Out__15bits(bin4_bin15_2_out__15bits));
  Bin4_bin15 bin4_bin15_3 (.In__4bits(bdois), .Out__15bits(bin4_bin15_3_out__15bits));
  Monta_barra monta_barra_2 (
    .In__Posicao_central_de_referencia_da_barra(bin4_bin15_3_out__15bits),
    .Out__barra_completa(monta_barra_2_out__barra_completa));
  Demultiplexer #(.select(4), .width(15), .enable("false")) demultiplexer_1 (
    .out1(demultiplexer_1_out1), .out2(demultiplexer_1_out2), .out3(demultiplexer_1_out3),
    .out4(demultiplexer_1_out4), .out5(demultiplexer_1_out5), .out6(demultiplexer_1_out6),
    .out7(demultiplexer_1_out7), .out8(demultiplexer_1_out8), .out9(demultiplexer_1_out9),
    .out10(demultiplexer_1_out10), .out11(demultiplexer_1_out11), .out12(demultiplexer_1_out12),
    .out13(demultiplexer_1_out13), .out14(demultiplexer_1_out14), .out15(demultiplexer_1_out15),
    .in(bin4_bin15_2_out__15bits), .sel(horizontal));  // open: out0
  Adder #(.width(15)) adder_1 (
    .a(monta_barra_1_out__barra_completa), .b(demultiplexer_1_out1), .out(adder_1_out));  // open: cin, cout
  Adder #(.width(15)) adder_2 (
    .a(demultiplexer_1_out15), .b(monta_barra_2_out__barra_completa), .out(adder_2_out));  // open: cin, cout
  Multiplexer #(.width(15), .enable("false")) multiplexer_1 (
    .in0(adder_1_out), .in1({15{1'b1}}), .out(zero), .sel(Acabou));
  Multiplexer #(.width(15), .enable("false")) multiplexer_2 (
    .in0(demultiplexer_1_out2), .in1({15{1'b1}}), .out(out_7), .sel(Acabou));
  Multiplexer #(.width(15), .enable("false")) multiplexer_3 (
    .in0(demultiplexer_1_out3), .in1({15{1'b1}}), .out(out_8), .sel(Acabou));
  Multiplexer #(.width(15), .enable("false")) multiplexer_4 (
    .in0(demultiplexer_1_out4), .in1({15{1'b1}}), .out(out_9), .sel(Acabou));
  Multiplexer #(.width(15), .enable("false")) multiplexer_5 (
    .in0(demultiplexer_1_out5), .in1({15{1'b1}}), .out(out_10), .sel(Acabou));
  Multiplexer #(.width(15), .enable("false")) multiplexer_6 (
    .in0(demultiplexer_1_out6), .in1({15{1'b1}}), .out(out_11), .sel(Acabou));
  Multiplexer #(.width(15), .enable("false")) multiplexer_7 (
    .in0(demultiplexer_1_out7), .in1({15{1'b1}}), .out(out_12), .sel(Acabou));
  Multiplexer #(.width(15), .enable("false")) multiplexer_8 (
    .in0(demultiplexer_1_out8), .in1({15{1'b1}}), .out(out_13), .sel(Acabou));
  Multiplexer #(.width(15), .enable("false")) multiplexer_9 (
    .in0(demultiplexer_1_out9), .in1({15{1'b1}}), .out(out_14), .sel(Acabou));
  Multiplexer #(.width(15), .enable("false")) multiplexer_10 (
    .in0(demultiplexer_1_out10), .in1({15{1'b1}}), .out(out_15), .sel(Acabou));
  Multiplexer #(.width(15), .enable("false")) multiplexer_11 (
    .in0(demultiplexer_1_out11), .in1({15{1'b1}}), .out(out_16), .sel(Acabou));
  Multiplexer #(.width(15), .enable("false")) multiplexer_12 (
    .in0(demultiplexer_1_out12), .in1({15{1'b1}}), .out(out_17), .sel(Acabou));
  Multiplexer #(.width(15), .enable("false")) multiplexer_13 (
    .in0(demultiplexer_1_out13), .in1({15{1'b1}}), .out(out_18), .sel(Acabou));
  Multiplexer #(.width(15), .enable("false")) multiplexer_14 (
    .in0(demultiplexer_1_out14), .in1({15{1'b1}}), .out(out_19), .sel(Acabou));
  Multiplexer #(.width(15), .enable("false")) multiplexer_15 (
    .in0(adder_2_out), .in1({15{1'b1}}), .out(quinze), .sel(Acabou));
endmodule

module Bin4_bin15 (
  input  [3:0] In__4bits,
  output [14:0] Out__15bits
);

  and and_1 (Out__15bits[0], In__4bits[0], ~In__4bits[1], ~In__4bits[2], ~In__4bits[3]);  // AND_Gate
  and and_2 (Out__15bits[1], ~In__4bits[0], In__4bits[1], ~In__4bits[2], ~In__4bits[3]);  // AND_Gate
  and and_3 (Out__15bits[2], In__4bits[0], In__4bits[1], ~In__4bits[2], ~In__4bits[3]);  // AND_Gate
  and and_4 (Out__15bits[3], ~In__4bits[0], ~In__4bits[1], In__4bits[2], ~In__4bits[3]);  // AND_Gate
  and and_5 (Out__15bits[4], In__4bits[0], ~In__4bits[1], In__4bits[2], ~In__4bits[3]);  // AND_Gate
  and and_6 (Out__15bits[5], ~In__4bits[0], In__4bits[1], In__4bits[2], ~In__4bits[3]);  // AND_Gate
  and and_7 (Out__15bits[6], In__4bits[0], In__4bits[1], In__4bits[2], ~In__4bits[3]);  // AND_Gate
  and and_8 (Out__15bits[7], ~In__4bits[0], ~In__4bits[1], ~In__4bits[2], In__4bits[3]);  // AND_Gate
  and and_9 (Out__15bits[8], In__4bits[0], ~In__4bits[1], ~In__4bits[2], In__4bits[3]);  // AND_Gate
  and and_10 (Out__15bits[9], ~In__4bits[0], In__4bits[1], ~In__4bits[2], In__4bits[3]);  // AND_Gate
  and and_11 (Out__15bits[10], In__4bits[0], In__4bits[1], ~In__4bits[2], In__4bits[3]);  // AND_Gate
  and and_12 (Out__15bits[11], ~In__4bits[0], ~In__4bits[1], In__4bits[2], In__4bits[3]);  // AND_Gate
  and and_13 (Out__15bits[12], In__4bits[0], ~In__4bits[1], In__4bits[2], In__4bits[3]);  // AND_Gate
  and and_14 (Out__15bits[13], ~In__4bits[0], In__4bits[1], In__4bits[2], In__4bits[3]);  // AND_Gate
  and and_15 (Out__15bits[14], In__4bits[0], In__4bits[1], In__4bits[2], In__4bits[3]);
endmodule

module Monta_barra (
  input  [14:0] In__Posicao_central_de_referencia_da_barra,
  output [14:0] Out__barra_completa
);

  buf or_1 (Out__barra_completa[0], In__Posicao_central_de_referencia_da_barra[1]);  // OR_Gate
  or or_2 (Out__barra_completa[1], In__Posicao_central_de_referencia_da_barra[1], In__Posicao_central_de_referencia_da_barra[2]);
  or or_3 (Out__barra_completa[2], In__Posicao_central_de_referencia_da_barra[1], In__Posicao_central_de_referencia_da_barra[2], In__Posicao_central_de_referencia_da_barra[3]);
  or or_4 (Out__barra_completa[3], In__Posicao_central_de_referencia_da_barra[4], In__Posicao_central_de_referencia_da_barra[2], In__Posicao_central_de_referencia_da_barra[3]);
  or or_5 (Out__barra_completa[4], In__Posicao_central_de_referencia_da_barra[3], In__Posicao_central_de_referencia_da_barra[4], In__Posicao_central_de_referencia_da_barra[5]);
  or or_6 (Out__barra_completa[5], In__Posicao_central_de_referencia_da_barra[4], In__Posicao_central_de_referencia_da_barra[5], In__Posicao_central_de_referencia_da_barra[6]);
  or or_7 (Out__barra_completa[6], In__Posicao_central_de_referencia_da_barra[5], In__Posicao_central_de_referencia_da_barra[6], In__Posicao_central_de_referencia_da_barra[7]);
  or or_8 (Out__barra_completa[7], In__Posicao_central_de_referencia_da_barra[6], In__Posicao_central_de_referencia_da_barra[7], In__Posicao_central_de_referencia_da_barra[8]);
  or or_9 (Out__barra_completa[8], In__Posicao_central_de_referencia_da_barra[7], In__Posicao_central_de_referencia_da_barra[8], In__Posicao_central_de_referencia_da_barra[9]);
  or or_10 (Out__barra_completa[9], In__Posicao_central_de_referencia_da_barra[8], In__Posicao_central_de_referencia_da_barra[9], In__Posicao_central_de_referencia_da_barra[10]);
  or or_11 (Out__barra_completa[10], In__Posicao_central_de_referencia_da_barra[9], In__Posicao_central_de_referencia_da_barra[10], In__Posicao_central_de_referencia_da_barra[11]);
  or or_12 (Out__barra_completa[11], In__Posicao_central_de_referencia_da_barra[10], In__Posicao_central_de_referencia_da_barra[11], In__Posicao_central_de_referencia_da_barra[12]);
  or or_13 (Out__barra_completa[12], In__Posicao_central_de_referencia_da_barra[11], In__Posicao_central_de_referencia_da_barra[12], In__Posicao_central_de_referencia_da_barra[13]);
  or or_14 (Out__barra_completa[13], In__Posicao_central_de_referencia_da_barra[12], In__Posicao_central_de_referencia_da_barra[13]);
  buf or_15 (Out__barra_completa[14], In__Posicao_central_de_referencia_da_barra[13]);  // OR_Gate
endmodule

module ControlaBola (
  input  Clock,
  input  [3:0] Barra1,
  input  [3:0] Barra2,
  input  Ligar,
  output [3:0] OUT_Horizontal,
  output PontoBarra2,
  output PontoBarra1,
  output [3:0] OUT_Vertical
);

  wire and_1_out, and_2_out, and_3_out, and_4_out, and_5_out, aumentavelocidade_1_out_clock__variavel,
       colisaocombarra1_1_colidiu, colisaocombarra2_1_colidiu, d_ff_1_q, d_ff_2_q, inversorentrada_1_out_3,
       multiplexer_3_out, multiplexer_4_out, or_1_out, or_2_out, randomiza_direcao_bola_1_out_2,
       randomiza_direcao_bola_1_out_3;
  wire [3:0] adder_1_out, adder_2_out, adder_3_out, adder_4_out, multiplexer_1_out, multiplexer_2_out,
       randomiza_pos_bola_1_random_x, randomiza_pos_bola_1_random_y, register_1_q, register_2_q;

  BateQuina batequina_1 (
    .vertical_bola(OUT_Vertical), .barra_1(Barra1), .horizontal_bola(OUT_Horizontal),
    .sentido_bola(d_ff_1_q), .\direção__bola (d_ff_2_q));  // open: out_6, out_7
  Randomiza_Pos_Bola randomiza_pos_bola_1 (
    .Clock(or_2_out), .random_x(randomiza_pos_bola_1_random_x), .random_y(randomiza_pos_bola_1_random_y));
  Randomiza_Direcao_Bola randomiza_direcao_bola_1 (
    .Clock(or_2_out), .out_2(randomiza_direcao_bola_1_out_2), .out_3(randomiza_direcao_bola_1_out_3));
  ColisaoComBarra1 colisaocombarra1_1 (
    .Horizontal(OUT_Horizontal), .VERTICAL(OUT_Vertical), .Barra(Barra1), .Colidiu(colisaocombarra1_1_colidiu));
  or or_1 (or_1_out, colisaocombarra1_1_colidiu, colisaocombarra2_1_colidiu);
  ColisaoComBarra2 colisaocombarra2_1 (
    .Horizontal(OUT_Horizontal), .VERTICAL(OUT_Vertical), .Barra(Barra2), .Colidiu(colisaocombarra2_1_colidiu));
  and and_1 (and_1_out, Ligar, ~PontoBarra2, ~PontoBarra1);  // AND_Gate
  Multiplexer #(.width(4), .enable("false")) multiplexer_1 (
    .in0(randomiza_pos_bola_1_random_x), .in1(OUT_Horizontal), .out(multiplexer_1_out), .sel(and_1_out));
  Multiplexer #(.width(4), .enable("false")) multiplexer_2 (
    .in0(randomiza_pos_bola_1_random_y), .in1(OUT_Vertical), .out(multiplexer_2_out), .sel(and_1_out));
  Register #(.width(4)) register_1 (
    .D(multiplexer_1_out), .Q(register_1_q), .clk(aumentavelocidade_1_out_clock__variavel));  // open: en, clr
  Register #(.width(4)) register_2 (
    .D(multiplexer_2_out), .Q(register_2_q), .clk(aumentavelocidade_1_out_clock__variavel));  // open: en, clr
  InversorEntrada inversorentrada_1 (.in_1(d_ff_1_q), .in_2(or_1_out), .out_3(inversorentrada_1_out_3));
  and and_2 (and_2_out, register_2_q[0], register_2_q[1], register_2_q[2], register_2_q[3]);
  and and_3 (and_3_out, register_2_q[0], ~register_2_q[1], ~register_2_q[2], ~register_2_q[3]);  // AND_Gate
  and and_4 (and_4_out, register_1_q[0], register_1_q[1], register_1_q[2], register_1_q[3]);
  and and_5 (and_5_out, register_1_q[0], ~register_1_q[1], ~register_1_q[2], ~register_1_q[3]);  // AND_Gate
  Multiplexer #(.enable("false")) multiplexer_3 (
    .in0(randomiza_direcao_bola_1_out_2), .in1(inversorentrada_1_out_3), .out(multiplexer_3_out),
    .sel(and_1_out));
  Multiplexer #(.enable("false")) multiplexer_4 (
    .in0(randomiza_direcao_bola_1_out_3), .in1(d_ff_2_q), .out(multiplexer_4_out), .sel(and_1_out));
  Adder #(.width(4)) adder_1 (.a(register_2_q), .b(4'b0001), .out(adder_1_out));  // open: cin, cout
  Adder #(.width(4)) adder_2 (.a(register_2_q), .b(4'b1111), .out(adder_2_out));  // open: cin, cout
  Adder #(.width(4)) adder_3 (.a(register_1_q), .b(4'b0001), .out(adder_3_out));  // open: cin, cout
  Adder #(.width(4)) adder_4 (.a(register_1_q), .b(4'b1111), .out(adder_4_out));  // open: cin, cout
  D_Flip_Flop d_ff_1 (
    .clk(aumentavelocidade_1_out_clock__variavel), .D(multiplexer_3_out), .Q(d_ff_1_q), .preset(and_4_out),
    .reset(and_5_out));  // open: Qn, en
  Multiplexer #(.width(4), .enable("false")) multiplexer_5 (
    .in0(adder_1_out), .in1(adder_2_out), .out(OUT_Vertical), .sel(d_ff_2_q));
  D_Flip_Flop d_ff_2 (
    .clk(aumentavelocidade_1_out_clock__variavel), .D(multiplexer_4_out), .Q(d_ff_2_q), .preset(and_2_out),
    .reset(and_3_out));  // open: Qn, en
  Multiplexer #(.width(4), .enable("false")) multiplexer_6 (
    .in0(adder_3_out), .in1(adder_4_out), .out(OUT_Horizontal), .sel(d_ff_1_q));
  MarcaPonto marcaponto_1 (.IN__Horizontal(OUT_Horizontal), .PontoBarra2(PontoBarra2), .PontoBarra1(PontoBarra1));
  or or_2 (or_2_out, PontoBarra1, PontoBarra2);
  AumentaVelocidade aumentavelocidade_1 (
    .Horizontal(OUT_Horizontal), .Clock(Clock), .Reiniciar(or_2_out),
    .OUT_CLOCK__VARIAVEL(aumentavelocidade_1_out_clock__variavel));
endmodule

module PegaTeclado (
  input  [6:0] In__7bits,
  input  Reset,
  input  Clock,
  output [3:0] Out__4bits
);

  wire and_1_out, and_2_out, and_3_out, and_4_out;
  wire [3:0] adder_1_out, adder_2_out, multiplexer_1_out, multiplexer_2_out, multiplexer_3_out,
       multiplexer_4_out;

  and and_1 (and_1_out, In__7bits[0], In__7bits[1], In__7bits[2], ~In__7bits[3], In__7bits[4], In__7bits[5], In__7bits[6], ~and_3_out);  // AND_Gate
  and and_2 (and_2_out, In__7bits[0], In__7bits[1], ~In__7bits[2], ~In__7bits[3], In__7bits[4], In__7bits[5], In__7bits[6], ~and_4_out);  // AND_Gate
  and and_3 (and_3_out, ~Out__4bits[0], Out__4bits[1], Out__4bits[2], Out__4bits[3]);  // AND_Gate
  and and_4 (and_4_out, ~Out__4bits[0], Out__4bits[1], ~Out__4bits[2], ~Out__4bits[3]);  // AND_Gate
  Multiplexer #(.width(4), .enable("false")) multiplexer_1 (
    .in1(4'b0001), .out(multiplexer_1_out), .sel(and_1_out));  // open: in0
  Multiplexer #(.width(4), .enable("false")) multiplexer_2 (
    .in1(4'b1111), .out(multiplexer_2_out), .sel(and_2_out));  // open: in0
  Adder #(.width(4)) adder_1 (.a(Out__4bits), .b(multiplexer_1_out), .out(adder_1_out));  // open: cin, cout
  Adder #(.width(4)) adder_2 (.a(Out__4bits), .b(multiplexer_2_out), .out(adder_2_out));  // open: cin, cout
  Multiplexer #(.width(4), .enable("false")) multiplexer_3 (
    .in0(adder_1_out), .in1(adder_2_out), .out(multiplexer_3_out), .sel(and_2_out));
  Multiplexer #(.width(4), .enable("false")) multiplexer_4 (
    .in0(multiplexer_3_out), .in1(4'b1000), .out(multiplexer_4_out), .sel(Reset));
  Register #(.width(4)) register_1 (.D(multiplexer_4_out), .Q(Out__4bits), .clk(Clock));  // open: en, clr
endmodule

module Comparador4bits (
  input  [3:0] in_1,
  input  [3:0] in_2,
  output out_3
);

  wire not_1_out, not_2_out, not_3_out, not_4_out, xor_1_out, xor_2_out, xor_3_out, xor_4_out;

  xor xor_1 (xor_1_out, in_1[0], in_2[0]);
  xor xor_2 (xor_2_out, in_1[1], in_2[1]);
  xor xor_3 (xor_3_out, in_1[2], in_2[2]);
  xor xor_4 (xor_4_out, in_1[3], in_2[3]);
  not not_1 (not_1_out, xor_1_out);
  not not_2 (not_2_out, xor_2_out);
  not not_3 (not_3_out, xor_3_out);
  not not_4 (not_4_out, xor_4_out);
  and and_1 (out_3, not_1_out, not_2_out, not_3_out, not_4_out);
endmodule

module InversorEntrada (
  input  in_1,
  input  in_2,
  output out_3
);

  wire and_1_out, and_2_out;

  and and_1 (and_1_out, ~in_1, in_2);  // AND_Gate
  and and_2 (and_2_out, ~in_2, in_1);  // AND_Gate
  or or_1 (out_3, and_1_out, and_2_out);
endmodule

module MarcaPonto (
  input  [3:0] IN__Horizontal,
  output PontoBarra2,
  output PontoBarra1
);

  and and_1 (PontoBarra2, IN__Horizontal[0], ~IN__Horizontal[1], ~IN__Horizontal[2], ~IN__Horizontal[3]);  // AND_Gate
  and and_2 (PontoBarra1, IN__Horizontal[0], IN__Horizontal[1], IN__Horizontal[2], IN__Horizontal[3]);
endmodule

module Placar (
  input  MarcarPonto,
  input  Clock,
  input  Reset,
  output Acabou_Venceu,
  output [2:0] PontosMarcados
);

  wire and_1_out, d_ff_1_q, d_ff_2_q;

  D_Flip_Flop d_ff_1 (.clk(Clock), .D(MarcarPonto), .Q(d_ff_1_q), .reset(d_ff_2_q));  // open: Qn, preset, en
  D_Flip_Flop d_ff_2 (.clk(Clock), .D(d_ff_1_q), .Q(d_ff_2_q), .preset(and_1_out));  // open: Qn, en, reset
  and and_1 (and_1_out, MarcarPonto, d_ff_2_q);
  Counter #(.width(3), .max('h7)) counter_1 (
    .count(d_ff_1_q), .Q(PontosMarcados), .clk(Clock), .clr(Reset));  // open: load, D, carry
  and and_2 (Acabou_Venceu, PontosMarcados[0], ~PontosMarcados[1], PontosMarcados[2]);  // AND_Gate
endmodule

module Display (
  input  [2:0] in_1,
  output A,
  output B,
  output C,
  output D,
  output E,
  output F,
  output G
);

  wire and_1_out, and_2_out, and_3_out, and_4_out, and_5_out, and_6_out, and_7_out, not_1_out, not_2_out,
       not_3_out, not_4_out, not_5_out, not_6_out, not_7_out, not_8_out, not_9_out, not_10_out, not_11_out,
       not_12_out;

  not not_1 (not_1_out, in_1[2]);
  not not_2 (not_2_out, in_1[0]);
  not not_3 (not_3_out, in_1[2]);
  not not_4 (not_4_out, in_1[0]);
  not not_5 (not_5_out, in_1[1]);
  not not_6 (not_6_out, in_1[2]);
  not not_7 (not_7_out, in_1[0]);
  not not_8 (not_8_out, in_1[2]);
  not not_9 (not_9_out, in_1[0]);
  not not_10 (not_10_out, in_1[0]);
  not not_11 (not_11_out, in_1[1]);
  not not_12 (not_12_out, in_1[0]);
  or or_1 (G, in_1[1], in_1[2]);
  and and_1 (and_1_out, not_1_out, not_2_out);
  and and_2 (and_2_out, in_1[2], in_1[0]);
  or or_2 (B, not_3_out, not_4_out, in_1[1]);
  or or_3 (C, not_5_out, in_1[0], in_1[2]);
  and and_3 (and_3_out, not_6_out, not_7_out);
  and and_4 (and_4_out, in_1[2], in_1[0]);
  and and_5 (and_5_out, not_8_out, not_9_out);
  and and_6 (and_6_out, in_1[1], not_10_out);
  and and_7 (and_7_out, not_11_out, not_12_out);
  or or_4 (A, and_1_out, in_1[1], and_2_out);
  or or_5 (D, and_3_out, in_1[1], and_4_out);
  or or_6 (E, and_5_out, and_6_out);
  or or_7 (F, and_7_out, in_1[2]);
endmodule

module IA (
  input  [3:0] bola_vertical,
  input  Clock,
  input  inicio,
  output [3:0] posicao_barra
);

  wire comparator_1_eq, comparator_2_eq, comparator_3_eq, subtractor_2_bout;
  wire [3:0] adder_1_out, adder_2_out, multiplexer_1_out, multiplexer_2_out, multiplexer_3_out,
       multiplexer_4_out, multiplexer_5_out, subtractor_1_out, subtractor_2_out, subtractor_3_out;

  // Probe on multiplexer_5_out
  // Probe on 4'b1111
  Adder #(.width(4)) adder_1 (.a(multiplexer_5_out), .b(4'b0001), .out(adder_1_out));  // open: cin, cout
  Comparator #(.width(4)) comparator_1 (.a(multiplexer_5_out), .b(4'b0001), .eq(comparator_1_eq));  // open: gt, lt
  Comparator #(.width(4)) comparator_2 (.a(multiplexer_1_out), .b(4'b1111), .eq(comparator_2_eq));  // open: gt, lt
  Multiplexer #(.width(4)) multiplexer_1 (
    .in0(multiplexer_5_out), .in1(adder_1_out), .out(multiplexer_1_out), .sel(comparator_1_eq));  // open: en
  // Probe on bola_vertical
  // Probe on posicao_barra
  // Probe on 4'b0111
  Subtractor #(.width(4)) subtractor_1 (.a(multiplexer_1_out), .b(4'b0001), .out(subtractor_1_out));  // open: bin, bout
  Subtractor #(.width(4)) subtractor_2 (
    .a(bola_vertical), .b(posicao_barra), .out(subtractor_2_out), .bout(subtractor_2_bout));  // open: bin
  Multiplexer #(.width(4)) multiplexer_2 (
    .in0(multiplexer_1_out), .in1(subtractor_1_out), .out(multiplexer_2_out), .sel(comparator_2_eq));  // open: en
  Comparator #(.width(4)) comparator_3 (.a(subtractor_2_out), .b(4'b0000), .eq(comparator_3_eq));  // open: gt, lt
  Register #(.width(4), .trigger("falling")) register_1 (
    .D(multiplexer_3_out), .Q(posicao_barra), .clk(Clock));  // open: en, clr
  Multiplexer #(.width(4)) multiplexer_3 (
    .in0(multiplexer_2_out), .in1(4'b0111), .out(multiplexer_3_out), .sel(inicio));  // open: en
  // Probe on multiplexer_3_out
  Adder #(.width(4)) adder_2 (.a(posicao_barra), .b(4'b0001), .out(adder_2_out));  // open: cin, cout
  Subtractor #(.width(4)) subtractor_3 (.a(posicao_barra), .b(4'b0001), .out(subtractor_3_out));  // open: bin, bout
  Multiplexer #(.width(4)) multiplexer_4 (
    .in0(adder_2_out), .in1(subtractor_3_out), .out(multiplexer_4_out), .sel(subtractor_2_bout));  // open: en
  // Probe on multiplexer_2_out
  Multiplexer #(.width(4)) multiplexer_5 (
    .in0(multiplexer_4_out), .in1(posicao_barra), .out(multiplexer_5_out), .sel(comparator_3_eq));  // open: en
endmodule

module ColisaoComBarra1 (
  input  [3:0] Horizontal,
  input  [3:0] VERTICAL,
  input  [3:0] Barra,
  output Colidiu
);

  wire and_1_out, comparador4bits_1_out_3, comparador4bits_2_out_3, comparador4bits_3_out_3, or_1_out;
  wire [3:0] adder_1_out, adder_2_out;

  Adder #(.width(4)) adder_1 (.a(4'b0001), .b(Barra), .out(adder_1_out));  // open: cin, cout
  Adder #(.width(4)) adder_2 (.a(Barra), .b(4'b1111), .out(adder_2_out));  // open: cin, cout
  and and_1 (and_1_out, ~Horizontal[0], Horizontal[1], ~Horizontal[2], ~Horizontal[3]);  // AND_Gate
  Comparador4bits comparador4bits_1 (.in_1(VERTICAL), .in_2(adder_1_out), .out_3(comparador4bits_1_out_3));
  Comparador4bits comparador4bits_2 (.in_1(VERTICAL), .in_2(Barra), .out_3(comparador4bits_2_out_3));
  Comparador4bits comparador4bits_3 (.in_1(VERTICAL), .in_2(adder_2_out), .out_3(comparador4bits_3_out_3));
  or or_1 (or_1_out, comparador4bits_3_out_3, comparador4bits_2_out_3, comparador4bits_1_out_3);
  and and_2 (Colidiu, and_1_out, or_1_out);
endmodule

module ColisaoComBarra2 (
  input  [3:0] Horizontal,
  input  [3:0] VERTICAL,
  input  [3:0] Barra,
  output Colidiu
);

  wire and_1_out, comparador4bits_1_out_3, comparador4bits_2_out_3, comparador4bits_3_out_3, or_1_out;
  wire [3:0] adder_1_out, adder_2_out;

  Adder #(.width(4)) adder_1 (.a(4'b0001), .b(Barra), .out(adder_1_out));  // open: cin, cout
  Adder #(.width(4)) adder_2 (.a(Barra), .b(4'b1111), .out(adder_2_out));  // open: cin, cout
  and and_1 (and_1_out, ~Horizontal[0], Horizontal[1], Horizontal[2], Horizontal[3]);  // AND_Gate
  Comparador4bits comparador4bits_1 (.in_1(VERTICAL), .in_2(adder_1_out), .out_3(comparador4bits_1_out_3));
  Comparador4bits comparador4bits_2 (.in_1(VERTICAL), .in_2(Barra), .out_3(comparador4bits_2_out_3));
  Comparador4bits comparador4bits_3 (.in_1(VERTICAL), .in_2(adder_2_out), .out_3(comparador4bits_3_out_3));
  or or_1 (or_1_out, comparador4bits_3_out_3, comparador4bits_2_out_3, comparador4bits_1_out_3);
  and and_2 (Colidiu, and_1_out, or_1_out);
endmodule

module Randomiza_Pos_Bola (
  input  Clock,
  output [3:0] random_x,
  output [3:0] random_y
);

  wire not_1_out, random_1_out;
  wire [1:0] multiplier_1_out, random_2_out;
  wire [3:0] negator_1_out, negator_2_out;

  not not_1 (not_1_out, Clock);
  Negator #(.width(4)) negator_1 (.in(4'b1001), .out(negator_1_out));
  Negator #(.width(4)) negator_2 (.in(4'b0110), .out(negator_2_out));
  Random #(.width(1)) random_1 (.clk(Clock), .out(random_1_out));  // open: next, clr
  Random #(.width(2)) random_2 (.clk(not_1_out), .out(random_2_out));  // open: next, clr
  Multiplier #(.width(2)) multiplier_1 (.a(random_2_out), .b(2'b11), .out(multiplier_1_out));  // open: cin, cout
  Multiplexer #(.width(4)) multiplexer_1 (.in0(4'b1000), .in1(4'b1001), .sel(random_1_out));  // open: out, en
  Multiplexer #(.select(2), .width(4)) multiplexer_2 (
    .in0(negator_1_out), .in1(4'b1000), .in2(4'b1001), .in3(negator_2_out), .out(random_y),
    .sel(multiplier_1_out));  // open: en

  assign random_x = 4'b1001;
endmodule

module Randomiza_Direcao_Bola (
  input  Clock,
  output out_2,
  output out_3
);

  wire and_1_out, random_2_out;

  Random #(.width(1)) random_1 (.clk(Clock), .out(out_2));  // open: next, clr
  Random #(.width(1)) random_2 (.clk(Clock), .out(random_2_out));  // open: next, clr
  Adder #(.width(1)) adder_1 (.a(random_2_out), .b(and_1_out), .out(out_3));  // open: cin, cout
  and and_1 (and_1_out, 1'b1, Clock);
endmodule

module AumentaVelocidade (
  input  [3:0] Horizontal,
  input  Clock,
  input  Reiniciar,
  output OUT_CLOCK__VARIAVEL
);

  wire and_1_out, and_2_out, and_3_out, and_4_out, and_5_out, clock_1_out, clock_2_out, clock_3_out,
       clock_4_out, d_ff_1_q, or_1_out, or_2_out;
  wire [1:0] counter_2_q;
  wire [3:0] counter_1_q;

  and and_1 (and_1_out, ~Horizontal[0], Horizontal[1], ~Horizontal[2], ~Horizontal[3]);  // AND_Gate
  and and_2 (and_2_out, ~Horizontal[0], Horizontal[1], Horizontal[2], Horizontal[3]);  // AND_Gate
  Clock #(.highDuration(32), .lowDuration(32)) clock_1 (.out(clock_1_out));
  Clock #(.highDuration(16), .lowDuration(16)) clock_2 (.out(clock_2_out));
  Clock #(.highDuration(8), .lowDuration(8)) clock_3 (.out(clock_3_out));
  Counter #(.width(4), .max('hf)) counter_1 (
    .count(or_1_out), .Q(counter_1_q), .clk(Clock), .clr(or_2_out));  // open: load, D, carry
  or or_1 (or_1_out, and_1_out, and_2_out);
  or or_2 (or_2_out, Reiniciar, d_ff_1_q);
  Clock #(.highDuration(64), .lowDuration(64)) clock_4 (.out(clock_4_out));
  D_Flip_Flop d_ff_1 (.clk(Clock), .D(and_3_out), .Q(d_ff_1_q));  // open: Qn, preset, en, reset
  Multiplexer #(.select(2)) multiplexer_1 (
    .in0(clock_4_out), .in1(clock_1_out), .in2(clock_2_out), .in3(clock_3_out), .out(OUT_CLOCK__VARIAVEL),
    .sel(counter_2_q));  // open: en
  and and_3 (and_3_out, ~counter_1_q[0], ~counter_1_q[1], counter_1_q[2], ~counter_1_q[3]);  // AND_Gate
  and and_4 (and_4_out, ~and_5_out, and_3_out);  // AND_Gate
  and and_5 (and_5_out, counter_2_q[1], counter_2_q[0]);
  Counter #(.width(2), .max('h3)) counter_2 (
    .count(and_4_out), .Q(counter_2_q), .clk(Clock), .clr(Reiniciar));  // open: load, D, carry
endmodule

module BateQuina (
  input  [3:0] vertical_bola,
  input  [3:0] barra_1,
  input  [3:0] horizontal_bola,
  input  sentido_bola,
  input  \direção__bola ,
  output out_6,
  output out_7
);

  wire and_1_out, comparator_1_eq, comparator_2_eq, comparator_3_eq, or_1_out, subtractor_1_bout;
  wire [3:0] subtractor_1_out;

  Comparator #(.width(4)) comparator_1 (.a(horizontal_bola), .b(4'b0010), .eq(comparator_1_eq));  // open: gt, lt
  // Probe on 4'b0010
  and and_1 (and_1_out, comparator_1_eq, or_1_out);
  InversorEntrada inversorentrada_1 (.in_1(sentido_bola), .in_2(and_1_out), .out_3(out_6));
  InversorEntrada inversorentrada_2 (.in_1(\direção__bola ), .in_2(and_1_out), .out_3(out_7));
  // Probe on subtractor_1_out
  Subtractor #(.width(4)) subtractor_1 (
    .a(vertical_bola), .b(barra_1), .out(subtractor_1_out), .bout(subtractor_1_bout));  // open: bin
  Comparator #(.width(4)) comparator_2 (.a(subtractor_1_out), .b(4'b0010), .eq(comparator_2_eq));  // open: gt, lt
  // Probe on subtractor_1_out
  Comparator #(.width(4)) comparator_3 (.a(subtractor_1_out), .b(4'b1111), .eq(comparator_3_eq));  // open: gt, lt
  or or_1 (or_1_out, comparator_2_eq, comparator_3_eq);
endmodule
