// Logisim project BinzaFULL.circ as structural Verilog: 6 circuits, main circuit quase main
module quase_main (
  input  [6:0] in_1,
  output [6:0] out_2,
  output _1,
  output _2,
  output [2:0] out_5,
  output _3,
  output _4,
  output _5,
  output _6,
  output out_10
);

  wire and_1_out, and_2_out, and_3_out, and_4_out, and_5_out, and_6_out, and_7_out, and_8_out, and_9_out,
       and_10_out, and_11_out, and_12_out, and_13_out, and_14_out, display1s_1_a, display1s_1_b,
       display1s_1_c, display1s_1_d, display1s_1_e, display1s_1_f, display1s_1_g, teste_1_a_2, teste_1_b_2,
       teste_1_c_2, teste_1_d_2, teste_1_e, teste_1_f, teste_1_g, testevogal_1_saidaevogal;

  Somade1s somade1s_1 (.Entrada__numero_a_ser_somado(in_1), .Saida__Soma_dos_1s(out_5));
  TesteVogal testevogal_1 (.Entrada_7_bits(in_1), .Saidaevogal(testevogal_1_saidaevogal));
  Display1s display1s_1 (
    .plus_significativo(out_5[2]), ._2(out_5[1]), ._1(out_5[0]), .a(display1s_1_a), .b(display1s_1_b),
    .c(display1s_1_c), .d(display1s_1_d), .e(display1s_1_e), .f(display1s_1_f), .g(display1s_1_g));
  teste teste_1 (
    .a(in_1[4]), .b(in_1[3]), .c(in_1[2]), .d(in_1[1]), .a_2(teste_1_a_2), .b_2(teste_1_b_2),
    .c_2(teste_1_c_2), .d_2(teste_1_d_2), .e(teste_1_e), .f(teste_1_f), .g(teste_1_g));
  and and_1 (and_1_out, display1s_1_a, ~testevogal_1_saidaevogal);  // AND_Gate
  and and_2 (and_2_out, display1s_1_b, ~testevogal_1_saidaevogal);  // AND_Gate
  and and_3 (and_3_out, display1s_1_c, ~testevogal_1_saidaevogal);  // AND_Gate
  and and_4 (and_4_out, display1s_1_d, ~testevogal_1_saidaevogal);  // AND_Gate
  and and_5 (and_5_out, display1s_1_e, ~testevogal_1_saidaevogal);  // AND_Gate
  and and_6 (and_6_out, display1s_1_f, ~testevogal_1_saidaevogal);  // AND_Gate
  and and_7 (and_7_out, display1s_1_g, ~testevogal_1_saidaevogal);  // AND_Gate
  buf and_8 (and_8_out, teste_1_a_2);  // AND_Gate
  and and_9 (and_9_out, teste_1_b_2, testevogal_1_saidaevogal);
  and and_10 (and_10_out, teste_1_c_2, testevogal_1_saidaevogal);
  and and_11 (and_11_out, teste_1_d_2, testevogal_1_saidaevogal);
  and and_12 (and_12_out, teste_1_e, testevogal_1_saidaevogal);
  and and_13 (and_13_out, teste_1_f, testevogal_1_saidaevogal);
  and and_14 (and_14_out, teste_1_g, testevogal_1_saidaevogal);
  or or_1 (_1, and_1_out, and_8_out);
  or or_2 (_2, and_2_out, and_9_out);
  or or_3 (_3, and_3_out, and_10_out);
  or or_4 (_4, and_4_out, and_11_out);
  or or_5 (_5, and_5_out, and_12_out);
  or or_6 (_6, and_6_out, and_13_out);
  or or_7 (out_10, and_7_out, and_14_out);

  assign out_2 = in_1;
endmodule

module teste (
  input  a,
  input  b,
  input  c,
  input  d,
  output a_2,
  output b_2,
  output c_2,
  output d_2,
  output e,
  output f,
  output g
);

  wire and_2_out, and_3_out, and_4_out, and_5_out, and_6_out, and_7_out, and_8_out, not_1_out, not_2_out,
       not_3_out, not_4_out, not_5_out, not_6_out, not_7_out, not_8_out, not_9_out, not_10_out, not_11_out,
       not_12_out, not_13_out, not_14_out;

  not not_1 (not_1_out, a);
  not not_2 (not_2_out, b);
  not not_3 (not_3_out, b);
  not not_4 (not_4_out, c);
  not not_5 (not_5_out, b);
  not not_6 (not_6_out, c);
  not not_7 (not_7_out, b);
  not not_8 (not_8_out, d);
  not not_9 (not_9_out, d);
  not not_10 (not_10_out, d);
  not not_11 (not_11_out, a);
  not not_12 (not_12_out, b);
  not not_13 (not_13_out, d);
  not not_14 (not_14_out, a);
  and and_1 (a_2, not_1_out, not_2_out);
  and and_2 (and_2_out, not_3_out, not_4_out);
  and and_3 (and_3_out, not_5_out, not_6_out);
  and and_4 (and_4_out, not_7_out, not_8_out);
  and and_5 (and_5_out, c, not_9_out);
  and and_6 (and_6_out, a, not_10_out);
  and and_7 (and_7_out, not_11_out, not_12_out, not_13_out);
  and and_8 (and_8_out, not_14_out, c);
  or or_1 (b_2, and_2_out, a);
  or or_2 (c_2, and_3_out, d, a);
  or or_3 (f, and_4_out, and_5_out, and_6_out);
  or or_4 (g, and_7_out, and_8_out);

  assign d_2 = c;
  assign e = 1'b1;
endmodule

module TesteVogal (
  input  [6:0] Entrada_7_bits,
  output Saidaevogal
);

  wire and_1_out, and_2_out, and_3_out, and_4_out, and_5_out, or_1_out;

  and and_1 (and_1_out, ~Entrada_7_bits[1], ~Entrada_7_bits[2], ~Entrada_7_bits[3], ~Entrada_7_bits[4]);  // AND_Gate
  and and_2 (and_2_out, ~Entrada_7_bits[4], ~Entrada_7_bits[3], ~Entrada_7_bits[1], Entrada_7_bits[2]);  // AND_Gate
  and and_3 (and_3_out, ~Entrada_7_bits[4], Entrada_7_bits[3], ~Entrada_7_bits[2], ~Entrada_7_bits[1]);  // AND_Gate
  and and_4 (and_4_out, ~Entrada_7_bits[4], Entrada_7_bits[3], Entrada_7_bits[2], Entrada_7_bits[1]);  // AND_Gate
  and and_5 (and_5_out, Entrada_7_bits[4], ~Entrada_7_bits[3], Entrada_7_bits[2], ~Entrada_7_bits[1]);  // AND_Gate
  or or_1 (or_1_out, and_1_out, and_2_out, and_3_out, and_4_out, and_5_out);
  and and_6 (Saidaevogal, or_1_out, Entrada_7_bits[0], Entrada_7_bits[5], Entrada_7_bits[6]);
endmodule

module Somade1s (
  input  [6:0] Entrada__numero_a_ser_somado,
  output [2:0] Saida__Soma_dos_1s
);

  wire [1:0] adder_1_out, adder_2_out, adder_3_out, adder_4_out, adder_5_out;
  wire [2:2] adder_4_cout, adder_5_cout;

  Adder #(.width(1)) adder_1 (
    .a(Entrada__numero_a_ser_somado[0]), .b(Entrada__numero_a_ser_somado[1]), .out(adder_1_out[0]),
    .cout(adder_1_out[1]));  // open: cin
  Adder #(.width(1)) adder_2 (
    .a(Entrada__numero_a_ser_somado[2]), .b(Entrada__numero_a_ser_somado[3]), .out(adder_2_out[0]),
    .cout(adder_2_out[1]));  // open: cin
  Adder #(.width(1)) adder_3 (
    .a(Entrada__numero_a_ser_somado[4]), .b(Entrada__numero_a_ser_somado[5]), .out(adder_3_out[0]),
    .cout(adder_3_out[1]));  // open: cin
  Adder #(.width(2)) adder_4 (
    .a(adder_1_out), .b(adder_2_out), .out(adder_4_out), .cout(adder_4_cout[2]));  // open: cin
  Adder #(.width(2)) adder_5 (
    .a(adder_3_out), .b({1'b0, Entrada__numero_a_ser_somado[6]}), .out(adder_5_out), .cout(adder_5_cout[2]));  // open: cin
  Adder #(.width(3)) adder_6 (
    .a({adder_4_cout[2], adder_4_out}), .b({adder_5_cout[2], adder_5_out}), .out(Saida__Soma_dos_1s));  // open: cin, cout
endmodule

module Display1s (
  input  plus_significativo,
  input  _2,
  input  _1,
  output a,
  output b,
  output c,
  output d,
  output e,
  output f,
  output g
);

  wire and_1_out, and_2_out, and_3_out, and_4_out, and_5_out, and_6_out, and_7_out, and_8_out, and_9_out,
       and_10_out, and_11_out, and_12_out, and_13_out, and_14_out, not_1_out, not_2_out, not_3_out,
       not_4_out, not_5_out, not_6_out, not_7_out, not_8_out, not_9_out, not_10_out, not_11_out, not_12_out,
       not_13_out, not_14_out, not_15_out, not_16_out, not_17_out, not_18_out;

  not not_1 (not_1_out, plus_significativo);
  not not_2 (not_2_out, _1);
  not not_3 (not_3_out, plus_significativo);
  not not_4 (not_4_out, _1);
  not not_5 (not_5_out, _2);
  not not_6 (not_6_out, _1);
  not not_7 (not_7_out, _2);
  not not_8 (not_8_out, _1);
  not not_9 (not_9_out, plus_significativo);
  not not_10 (not_10_out, _1);
  not not_11 (not_11_out, plus_significativo);
  not not_12 (not_12_out, _1);
  not not_13 (not_13_out, _2);
  not not_14 (not_14_out, plus_significativo);
  not not_15 (not_15_out, _2);
  not not_16 (not_16_out, _1);
  not not_17 (not_17_out, _1);
  or or_1 (g, _2, plus_significativo);
  and and_1 (and_1_out, not_1_out, not_2_out);
  and and_2 (and_2_out, plus_significativo, _1);
  and and_3 (and_3_out, not_3_out, not_4_out);
  and and_4 (and_4_out, not_5_out, not_6_out);
  and and_5 (and_5_out, _2, _1);
  and and_6 (and_6_out, not_7_out, not_8_out);
  and and_7 (and_7_out, _2, _1);
  and and_8 (and_8_out, not_9_out, not_10_out);
  and and_9 (and_9_out, not_11_out, _2);
  and and_10 (and_10_out, _2, not_12_out);
  and and_11 (and_11_out, plus_significativo, not_13_out, _1);
  and and_12 (and_12_out, not_14_out, not_15_out);
  and and_13 (and_13_out, _2, not_16_out);
  not not_18 (not_18_out, _2);
  and and_14 (and_14_out, plus_significativo, not_17_out);
  or or_2 (a, and_1_out, _2, and_2_out);
  or or_3 (b, and_3_out, and_4_out, and_5_out);
  or or_4 (c, and_6_out, and_7_out, plus_significativo);
  or or_5 (d, and_8_out, and_9_out, and_10_out, and_11_out);
  or or_6 (e, and_12_out, and_13_out);
  or or_7 (f, not_18_out, and_14_out);
endmodule

module PROJETO_FINALIZADO (
  input  in_1
);

  wire quase_main_1__1, quase_main_1__2, quase_main_1__3, quase_main_1__4, quase_main_1__5, quase_main_1__6,
       quase_main_1_out_10;
  wire [6:0] keyboard_1_data;

  Keyboard keyboard_1 (.re(in_1), .clr(in_1), .data(keyboard_1_data));  // open: clk, avail
  // Probe on keyboard_1_data
  quase_main quase_main_1 (
    .in_1(keyboard_1_data), ._1(quase_main_1__1), ._2(quase_main_1__2), ._3(quase_main_1__3),
    ._4(quase_main_1__4), ._5(quase_main_1__5), ._6(quase_main_1__6), .out_10(quase_main_1_out_10));  // open: out_2, out_5
  _7_Segment_Display u_7_segment_display_1 (
    .g(quase_main_1_out_10), .f(quase_main_1__6), .a(quase_main_1__1), .b(quase_main_1__2),
    .e(quase_main_1__5), .d(quase_main_1__4), .c(quase_main_1__3));  // open: dp
endmodule
