// Logisim project Jogo_do_Tiro_Espacial.circ as structural Verilog: 7 circuits, main circuit main
module main (
  input  in_1,
  output [6:0] out_2
);

  wire botaoativado_1_a, botaoativado_1_d, botaoativado_1_w, clock_1_out, clock_2_out, letra_binario_1_lsb2,
       letra_binario_1_msb;
  wire [9:0] controlabarrinhatiro_1_out_6, controlabarrinhatiro_1_out_7, controlabarrinhatiro_1_out_8,
       controlabarrinhatiro_1_out_9, controlabarrinhatiro_1_out_10, controlabarrinhatiro_1_out_11,
       controlabarrinhatiro_1_out_12, controlabarrinhatiro_1_out_13, controlabarrinhatiro_1_out_14,
       controlabarrinhatiro_1_out_15;

  Clock clock_1 (.out(clock_1_out));
  Keyboard keyboard_1 (.clk(clock_1_out), .re(in_1), .data(out_2));  // open: clr, avail
  Clock #(.highDuration(4), .lowDuration(4)) clock_2 (.out(clock_2_out));
  DotMatrix #(.matrixcols(10), .matrixrows(10)) dotmatrix_1 (
    .col0(controlabarrinhatiro_1_out_6), .col1(controlabarrinhatiro_1_out_7),
    .col2(controlabarrinhatiro_1_out_8), .col3(controlabarrinhatiro_1_out_9),
    .col4(controlabarrinhatiro_1_out_10), .col5(controlabarrinhatiro_1_out_11),
    .col6(controlabarrinhatiro_1_out_12), .col7(controlabarrinhatiro_1_out_13),
    .col8(controlabarrinhatiro_1_out_14), .col9(controlabarrinhatiro_1_out_15));
  ControlaBarrinhaTiro controlabarrinhatiro_1 (
    .A(botaoativado_1_a), .D(botaoativado_1_d), .W(botaoativado_1_w), .ClockBarra(clock_1_out),
    .ClockTiro(clock_2_out), .out_6(controlabarrinhatiro_1_out_6), .out_7(controlabarrinhatiro_1_out_7),
    .out_8(controlabarrinhatiro_1_out_8), .out_9(controlabarrinhatiro_1_out_9),
    .out_10(controlabarrinhatiro_1_out_10), .out_11(controlabarrinhatiro_1_out_11),
    .out_12(controlabarrinhatiro_1_out_12), .out_13(controlabarrinhatiro_1_out_13),
    .out_14(controlabarrinhatiro_1_out_14), .out_15(controlabarrinhatiro_1_out_15));
  BotaoAtivado botaoativado_1 (
    .Menor(letra_binario_1_lsb2), .Maior(letra_binario_1_msb), .A(botaoativado_1_a), .D(botaoativado_1_d),
    .W(botaoativado_1_w));
  Letra_binario letra_binario_1 (
    .LSB(out_2[0]), .a(out_2[1]), .b(out_2[2]), .c(out_2[3]), .MSB2(out_2[4]), .LSB2(letra_binario_1_lsb2),
    .MSB(letra_binario_1_msb));
endmodule

module Letra_binario (
  input  LSB,
  input  a,
  input  b,
  input  c,
  input  MSB2,
  output LSB2,
  output MSB
);

  wire and_1_out, and_2_out, and_3_out, and_4_out, not_1_out, not_2_out, not_3_out, not_4_out, not_5_out,
       not_6_out, not_7_out, not_8_out, not_9_out, not_10_out, not_11_out, not_12_out, not_13_out;

  not not_1 (not_1_out, LSB);
  not not_2 (not_2_out, a);
  not not_3 (not_3_out, c);
  not not_4 (not_4_out, MSB2);
  not not_5 (not_5_out, a);
  not not_6 (not_6_out, b);
  not not_7 (not_7_out, c);
  not not_8 (not_8_out, MSB2);
  not not_9 (not_9_out, LSB);
  not not_10 (not_10_out, a);
  not not_11 (not_11_out, c);
  not not_12 (not_12_out, MSB2);
  not not_13 (not_13_out, c);
  and and_1 (and_1_out, not_1_out, not_2_out, b, not_3_out, not_4_out);
  and and_2 (and_2_out, LSB, not_5_out, not_6_out, not_7_out, not_8_out);
  and and_3 (and_3_out, not_9_out, not_10_out, b, not_11_out, not_12_out);
  and and_4 (and_4_out, LSB, a, b, not_13_out, MSB2);
  or or_1 (LSB2, and_1_out, and_2_out);
  or or_2 (MSB, and_3_out, and_4_out);
endmodule

module ControlaBarrinha (
  input  clk,
  input  Esquerda,
  input  Direita,
  output [9:0] out_4,
  output [9:0] out_5,
  output [9:0] out_6,
  output [9:0] out_7,
  output [3:0] Centro,
  output [9:0] out_9,
  output [9:0] out_10,
  output [9:0] out_11,
  output [9:0] out_12,
  output [9:0] out_13,
  output [9:0] out_14
);

  wire and_1_out, and_3_out, not_1_out, not_2_out, numeropixel_1_dez, numeropixel_1_s, numeropixel_1_t,
       numeropixel_1_u, numeropixel_1_um, numeropixel_1_v, numeropixel_1_w, numeropixel_1_x, numeropixel_1_y,
       numeropixel_1_z, numeropixel_2_dez, numeropixel_2_s, numeropixel_2_t, numeropixel_2_u,
       numeropixel_2_um, numeropixel_2_v, numeropixel_2_w, numeropixel_2_x, numeropixel_2_y, numeropixel_2_z,
       numeropixel_3_dez, numeropixel_3_s, numeropixel_3_t, numeropixel_3_u, numeropixel_3_um,
       numeropixel_3_v, numeropixel_3_w, numeropixel_3_x, numeropixel_3_y, numeropixel_3_z, or_1_out,
       or_2_out, or_3_out, or_4_out, or_5_out, or_6_out, or_7_out, or_8_out, or_9_out, or_10_out;
  wire [0:0] and_2_out;
  wire [3:0] adder_1_out, adder_2_out, adder_4_out, multiplexer_1_out, register_1_q;
  wire [3:3] and_4_out;

  not not_1 (not_1_out, and_1_out);
  and and_1 (and_1_out, or_9_out, or_10_out, ~or_8_out);  // AND_Gate
  and and_2 (and_2_out[0], Direita, not_1_out);
  not not_2 (not_2_out, and_3_out);
  and and_3 (and_3_out, ~or_3_out, or_2_out, or_1_out);  // AND_Gate
  and and_4 (and_4_out[3], Esquerda, not_2_out);
  Adder #(.width(4)) adder_1 (.a(register_1_q), .b({3'b000, and_2_out[0]}), .out(adder_1_out));  // open: cin, cout
  Adder #(.width(4)) adder_2 (.a(register_1_q), .b({4{and_4_out[3]}}), .out(adder_2_out));  // open: cin, cout
  // Probe on {4{and_4_out[3]}}
  Register #(.width(4)) register_1 (.D(multiplexer_1_out), .Q(register_1_q), .clk(clk));  // open: en, clr
  // Probe on multiplexer_1_out
  Multiplexer #(.width(4)) multiplexer_1 (
    .in0(adder_1_out), .in1(adder_2_out), .out(multiplexer_1_out), .sel(and_4_out[3]));  // open: en
  // Probe on register_1_q
  Adder #(.width(4)) adder_3 (.a(4'b0001), .b(register_1_q), .out(Centro));  // open: cin, cout
  // Probe on Centro
  Adder #(.width(4)) adder_4 (.a(4'b0010), .b(register_1_q), .out(adder_4_out));  // open: cin, cout
  // Probe on adder_4_out
  NumeroPixel numeropixel_1 (
    .Menor(adder_4_out[0]), .b(adder_4_out[1]), .a(adder_4_out[2]), .Maior(adder_4_out[3]),
    .um(numeropixel_1_um), .x(numeropixel_1_x), .y(numeropixel_1_y), .z(numeropixel_1_z),
    .u(numeropixel_1_u), .v(numeropixel_1_v), .w(numeropixel_1_w), .s(numeropixel_1_s), .t(numeropixel_1_t),
    .dez(numeropixel_1_dez));
  NumeroPixel numeropixel_2 (
    .Menor(Centro[0]), .b(Centro[1]), .a(Centro[2]), .Maior(Centro[3]), .um(numeropixel_2_um),
    .x(numeropixel_2_x), .y(numeropixel_2_y), .z(numeropixel_2_z), .u(numeropixel_2_u), .v(numeropixel_2_v),
    .w(numeropixel_2_w), .s(numeropixel_2_s), .t(numeropixel_2_t), .dez(numeropixel_2_dez));
  NumeroPixel numeropixel_3 (
    .Menor(register_1_q[0]), .b(register_1_q[1]), .a(register_1_q[2]), .Maior(register_1_q[3]),
    .um(numeropixel_3_um), .x(numeropixel_3_x), .y(numeropixel_3_y), .z(numeropixel_3_z),
    .u(numeropixel_3_u), .v(numeropixel_3_v), .w(numeropixel_3_w), .s(numeropixel_3_s), .t(numeropixel_3_t),
    .dez(numeropixel_3_dez));
  or or_1 (or_1_out, numeropixel_3_um, numeropixel_2_um, numeropixel_1_um);
  or or_2 (or_2_out, numeropixel_3_x, numeropixel_2_x, numeropixel_1_x);
  or or_3 (or_3_out, numeropixel_3_y, numeropixel_2_y, numeropixel_1_y);
  or or_4 (or_4_out, numeropixel_3_z, numeropixel_2_z, numeropixel_1_z);
  or or_5 (or_5_out, numeropixel_3_u, numeropixel_2_u, numeropixel_1_u);
  or or_6 (or_6_out, numeropixel_3_v, numeropixel_2_v, numeropixel_1_v);
  or or_7 (or_7_out, numeropixel_3_w, numeropixel_2_w, numeropixel_1_w);
  or or_8 (or_8_out, numeropixel_3_s, numeropixel_2_s, numeropixel_1_s);
  or or_9 (or_9_out, numeropixel_3_t, numeropixel_2_t, numeropixel_1_t);
  or or_10 (or_10_out, numeropixel_3_dez, numeropixel_2_dez, numeropixel_1_dez);
  assign out_7 = {{9{1'b0}}, or_4_out};  // Bit_Extender bit_extender_1
  assign out_9 = {{9{1'b0}}, or_5_out};  // Bit_Extender bit_extender_2
  assign out_10 = {{9{1'b0}}, or_6_out};  // Bit_Extender bit_extender_3
  assign out_11 = {{9{1'b0}}, or_7_out};  // Bit_Extender bit_extender_4
  assign out_12 = {{9{1'b0}}, or_8_out};  // Bit_Extender bit_extender_5
  assign out_13 = {{9{1'b0}}, or_9_out};  // Bit_Extender bit_extender_6
  assign out_14 = {{9{1'b0}}, or_10_out};  // Bit_Extender bit_extender_7
  assign out_4 = {{9{1'b0}}, or_1_out};  // Bit_Extender bit_extender_8
  assign out_5 = {{9{1'b0}}, or_2_out};  // Bit_Extender bit_extender_9
  assign out_6 = {{9{1'b0}}, or_3_out};  // Bit_Extender bit_extender_10
endmodule

module NumeroPixel (
  input  Menor,
  input  b,
  input  a,
  input  Maior,
  output um,
  output x,
  output y,
  output z,
  output u,
  output v,
  output w,
  output s,
  output t,
  output dez
);

  wire not_1_out, not_2_out, not_3_out, not_4_out, not_5_out, not_6_out, not_7_out, not_8_out, not_9_out,
       not_10_out, not_11_out, not_12_out, not_13_out, not_14_out, not_15_out, not_16_out, not_17_out,
       not_18_out, not_19_out, not_20_out, not_21_out, not_22_out, not_23_out;

  not not_1 (not_1_out, Maior);
  not not_2 (not_2_out, a);
  not not_3 (not_3_out, b);
  not not_4 (not_4_out, Maior);
  not not_5 (not_5_out, a);
  not not_6 (not_6_out, Menor);
  not not_7 (not_7_out, Maior);
  not not_8 (not_8_out, a);
  not not_9 (not_9_out, Maior);
  not not_10 (not_10_out, b);
  not not_11 (not_11_out, Menor);
  not not_12 (not_12_out, Maior);
  not not_13 (not_13_out, b);
  not not_14 (not_14_out, Maior);
  not not_15 (not_15_out, Menor);
  not not_16 (not_16_out, Maior);
  not not_17 (not_17_out, a);
  not not_18 (not_18_out, b);
  not not_19 (not_19_out, Menor);
  not not_20 (not_20_out, a);
  not not_21 (not_21_out, b);
  not not_22 (not_22_out, a);
  not not_23 (not_23_out, Menor);
  and and_1 (um, not_1_out, not_2_out, not_3_out, Menor);
  and and_2 (x, not_4_out, not_5_out, b, not_6_out);
  and and_3 (y, not_7_out, not_8_out, b, Menor);
  and and_4 (z, not_9_out, a, not_10_out, not_11_out);
  and and_5 (u, not_12_out, a, not_13_out, Menor);
  and and_6 (v, not_14_out, a, b, not_15_out);
  and and_7 (w, not_16_out, a, b, Menor);
  and and_8 (s, Maior, not_17_out, not_18_out, not_19_out);
  and and_9 (t, Maior, not_20_out, not_21_out, Menor);
  and and_10 (dez, Maior, not_22_out, b, not_23_out);
endmodule

module BotaoAtivado (
  input  Menor,
  input  Maior,
  output A,
  output D,
  output W
);

  and and_1 (A, Menor, ~Maior);  // AND_Gate
  and and_2 (D, Menor, Maior);
  and and_3 (W, Maior, ~Menor);  // AND_Gate
endmodule

module ControlaTiro (
  input  [9:0] Entrada,
  input  Ativar,
  input  W,
  input  ClockAssincrono,
  output [9:0] Saida
);

  wire and_1_out, and_2_out, d_ff_1_q;
  wire [3:0] adder_1_out, register_1_q;

  D_Flip_Flop d_ff_1 (.clk(ClockAssincrono), .Q(d_ff_1_q), .preset(and_1_out), .reset(and_2_out));  // open: D, Qn, en
  and and_1 (and_1_out, Ativar, W);
  Adder #(.width(4)) adder_1 (.a(register_1_q), .b(4'b0001), .out(adder_1_out));  // open: cin, cout
  Register #(.width(4)) register_1 (
    .D(adder_1_out), .en(d_ff_1_q), .Q(register_1_q), .clk(ClockAssincrono), .clr(and_2_out));
  NumeroPixel numeropixel_1 (
    .Menor(register_1_q[0]), .b(register_1_q[1]), .a(register_1_q[2]), .Maior(register_1_q[3]), .x(Saida[1]),
    .y(Saida[2]), .z(Saida[3]), .u(Saida[4]), .v(Saida[5]), .w(Saida[6]), .s(Saida[7]), .t(Saida[8]),
    .dez(Saida[9]));  // open: um
  and and_2 (and_2_out, register_1_q[0], register_1_q[1], ~register_1_q[2], register_1_q[3]);  // AND_Gate

  assign Saida[0] = Entrada[0];
endmodule

module ControlaBarrinhaTiro (
  input  A,
  input  D,
  input  W,
  input  ClockBarra,
  input  ClockTiro,
  output [9:0] out_6,
  output [9:0] out_7,
  output [9:0] out_8,
  output [9:0] out_9,
  output [9:0] out_10,
  output [9:0] out_11,
  output [9:0] out_12,
  output [9:0] out_13,
  output [9:0] out_14,
  output [9:0] out_15
);

  wire numeropixel_1_dez, numeropixel_1_s, numeropixel_1_t, numeropixel_1_u, numeropixel_1_um,
       numeropixel_1_v, numeropixel_1_w, numeropixel_1_x, numeropixel_1_y, numeropixel_1_z;
  wire [3:0] controlabarrinha_1_centro;
  wire [9:0] controlabarrinha_1_out_4, controlabarrinha_1_out_5, controlabarrinha_1_out_6,
       controlabarrinha_1_out_7, controlabarrinha_1_out_9, controlabarrinha_1_out_10,
       controlabarrinha_1_out_11, controlabarrinha_1_out_12, controlabarrinha_1_out_13,
       controlabarrinha_1_out_14;

  NumeroPixel numeropixel_1 (
    .Menor(controlabarrinha_1_centro[0]), .b(controlabarrinha_1_centro[1]), .a(controlabarrinha_1_centro[2]),
    .Maior(controlabarrinha_1_centro[3]), .um(numeropixel_1_um), .x(numeropixel_1_x), .y(numeropixel_1_y),
    .z(numeropixel_1_z), .u(numeropixel_1_u), .v(numeropixel_1_v), .w(numeropixel_1_w), .s(numeropixel_1_s),
    .t(numeropixel_1_t), .dez(numeropixel_1_dez));
  ControlaTiro controlatiro_1 (
    .Entrada(controlabarrinha_1_out_4), .W(W), .ClockAssincrono(ClockTiro), .Ativar(numeropixel_1_um),
    .Saida(out_6));
  ControlaTiro controlatiro_2 (
    .Entrada(controlabarrinha_1_out_5), .W(W), .ClockAssincrono(ClockTiro), .Ativar(numeropixel_1_x),
    .Saida(out_7));
  ControlaBarrinha controlabarrinha_1 (
    .clk(ClockBarra), .Esquerda(A), .Direita(D), .Centro(controlabarrinha_1_centro),
    .out_4(controlabarrinha_1_out_4), .out_5(controlabarrinha_1_out_5), .out_6(controlabarrinha_1_out_6),
    .out_7(controlabarrinha_1_out_7), .out_9(controlabarrinha_1_out_9), .out_10(controlabarrinha_1_out_10),
    .out_11(controlabarrinha_1_out_11), .out_12(controlabarrinha_1_out_12),
    .out_13(controlabarrinha_1_out_13), .out_14(controlabarrinha_1_out_14));
  ControlaTiro controlatiro_3 (
    .Entrada(controlabarrinha_1_out_6), .W(W), .ClockAssincrono(ClockTiro), .Ativar(numeropixel_1_y),
    .Saida(out_8));
  ControlaTiro controlatiro_4 (
    .Entrada(controlabarrinha_1_out_7), .W(W), .ClockAssincrono(ClockTiro), .Ativar(numeropixel_1_z),
    .Saida(out_9));
  ControlaTiro controlatiro_5 (
    .Entrada(controlabarrinha_1_out_9), .W(W), .ClockAssincrono(ClockTiro), .Ativar(numeropixel_1_u),
    .Saida(out_10));
  ControlaTiro controlatiro_6 (
    .Entrada(controlabarrinha_1_out_10), .W(W), .ClockAssincrono(ClockTiro), .Ativar(numeropixel_1_v),
    .Saida(out_11));
  ControlaTiro controlatiro_7 (
    .Entrada(controlabarrinha_1_out_11), .W(W), .ClockAssincrono(ClockTiro), .Ativar(numeropixel_1_w),
    .Saida(out_12));
  ControlaTiro controlatiro_8 (
    .Entrada(controlabarrinha_1_out_12), .W(W), .ClockAssincrono(ClockTiro), .Ativar(numeropixel_1_s),
    .Saida(out_13));
  ControlaTiro controlatiro_9 (
    .Entrada(controlabarrinha_1_out_13), .W(W), .ClockAssincrono(ClockTiro), .Ativar(numeropixel_1_t),
    .Saida(out_14));
  ControlaTiro controlatiro_10 (
    .Entrada(controlabarrinha_1_out_14), .W(W), .ClockAssincrono(ClockTiro), .Ativar(numeropixel_1_dez),
    .Saida(out_15));
endmodule
