// Logisim project MENOR EM X.circ as structural Verilog: 1 circuit, main circuit main
module main (
  output [3:0] out_1,
  output [3:0] out_2,
  output [3:0] out_3,
  output [3:0] out_4,
  output [3:0] random_x,
  output [3:0] random_y
);

  wire clock_1_out, not_1_out, random_1_out;
  wire [1:0] multiplier_1_out, random_2_out;

  Clock clock_1 (.out(clock_1_out));
  Random #(.width(1)) random_1 (.clk(clock_1_out), .out(random_1_out));  // open: next, clr
  not not_1 (not_1_out, clock_1_out);
  Random #(.width(2)) random_2 (.clk(not_1_out), .out(random_2_out));  // open: next, clr
  Negator #(.width(4)) negator_1 (.in(4'b1001), .out(out_1));
  Negator #(.width(4)) negator_2 (.in(4'b0110), .out(out_4));
  Multiplexer #(.width(4)) multiplexer_1 (
    .in0(4'b1000), .in1(4'b1001), .out(random_x), .sel(random_1_out));  // open: en
  Multiplexer #(.select(2), .width(4)) multiplexer_2 (
    .in0(out_1), .in1(4'b1000), .in2(4'b1001), .in3(out_4), .out(random_y), .sel(multiplier_1_out));  // open: en
  Multiplier #(.width(2)) multiplier_1 (.a(random_2_out), .b(2'b11), .out(multiplier_1_out));  // open: cin, cout

  assign out_2 = 4'b1000;
  assign out_3 = 4'b1001;
endmodule
