// Logisim project OS CALISTENICOS.circ as structural Verilog: 2 circuits, main circuit main
module main (
  input  a,
  input  b,
  input  c,
  input  d,
  output x,
  output y,
  output z,
  output u,
  output v,
  output w,
  output s
);

  wire and_1_out, and_2_out, and_3_out, and_4_out, and_5_out, and_6_out, and_7_out, and_8_out, and_9_out,
       and_10_out, and_11_out, and_12_out, and_13_out, and_14_out, and_15_out, and_16_out, and_17_out,
       and_18_out, and_19_out, and_20_out, and_21_out, and_22_out, and_23_out, and_24_out, and_25_out,
       and_26_out, and_27_out, and_28_out, not_1_out, not_2_out, not_3_out, not_4_out, not_5_out, not_6_out,
       not_7_out, not_8_out, not_9_out, not_10_out, not_11_out, not_12_out, not_13_out, not_14_out,
       not_15_out, not_16_out, not_17_out, not_18_out, not_19_out, not_20_out, not_21_out, not_22_out,
       not_23_out, not_24_out, not_25_out, not_26_out, not_27_out, not_28_out, not_29_out, not_30_out,
       not_31_out, not_32_out, not_33_out, not_34_out, not_35_out, not_36_out, not_37_out, not_38_out,
       not_39_out, not_40_out, not_41_out, not_42_out, not_43_out, not_44_out;

  not not_1 (not_1_out, a);
  and and_1 (and_1_out, not_1_out, not_2_out, not_3_out);
  not not_2 (not_2_out, b);
  not not_3 (not_3_out, c);
  not not_4 (not_4_out, a);
  not not_5 (not_5_out, c);
  and and_2 (and_2_out, not_4_out, not_5_out, not_6_out);
  not not_6 (not_6_out, d);
  not not_7 (not_7_out, a);
  and and_3 (and_3_out, not_7_out, c, d);
  and and_4 (and_4_out, a, not_8_out, d);
  not not_8 (not_8_out, c);
  and and_5 (and_5_out, a, b, not_9_out);
  not not_9 (not_9_out, d);
  not not_10 (not_10_out, a);
  not not_11 (not_11_out, c);
  not not_12 (not_12_out, d);
  not not_13 (not_13_out, c);
  not not_14 (not_14_out, d);
  not not_15 (not_15_out, a);
  not not_16 (not_16_out, b);
  not not_17 (not_17_out, c);
  not not_18 (not_18_out, a);
  not not_19 (not_19_out, c);
  not not_20 (not_20_out, d);
  not not_21 (not_21_out, a);
  not not_22 (not_22_out, b);
  not not_23 (not_23_out, d);
  not not_24 (not_24_out, c);
  not not_25 (not_25_out, b);
  and and_6 (and_6_out, not_25_out, not_26_out);
  not not_26 (not_26_out, c);
  not not_27 (not_27_out, a);
  and and_7 (and_7_out, not_27_out, d);
  and and_8 (and_8_out, a, not_28_out);
  not not_28 (not_28_out, c);
  and and_9 (and_9_out, a, b, not_29_out);
  not not_29 (not_29_out, d);
  not not_30 (not_30_out, c);
  and and_10 (and_10_out, not_30_out, not_31_out);
  not not_31 (not_31_out, d);
  not not_32 (not_32_out, b);
  and and_11 (and_11_out, not_32_out, c, d);
  and and_12 (and_12_out, b, not_33_out);
  not not_33 (not_33_out, c);
  and and_13 (and_13_out, b, not_34_out);
  not not_34 (not_34_out, d);
  and and_14 (and_14_out, a, not_35_out);
  not not_35 (not_35_out, b);
  not not_36 (not_36_out, c);
  not not_37 (not_37_out, b);
  and and_15 (and_15_out, not_37_out, d);
  not not_38 (not_38_out, a);
  and and_16 (and_16_out, not_38_out, b);
  not not_39 (not_39_out, b);
  not not_40 (not_40_out, c);
  not not_41 (not_41_out, a);
  not not_42 (not_42_out, b);
  not not_43 (not_43_out, c);
  not not_44 (not_44_out, d);
  or or_1 (x, and_1_out, and_2_out, and_3_out, and_4_out, and_5_out);
  and and_17 (and_17_out, not_10_out, not_11_out, not_12_out);
  and and_18 (and_18_out, a, b, not_13_out, d);
  or or_2 (y, and_17_out, and_18_out, and_19_out);
  and and_19 (and_19_out, a, b, c, not_14_out);
  and and_20 (and_20_out, not_15_out, not_16_out, not_17_out);
  and and_21 (and_21_out, not_18_out, not_19_out, not_20_out);
  and and_22 (and_22_out, not_21_out, b, c, d);
  and and_23 (and_23_out, a, not_22_out, c, not_23_out);
  and and_24 (and_24_out, a, b, not_24_out, d);
  or or_3 (u, and_6_out, and_7_out, and_8_out, and_9_out);
  or or_4 (v, and_10_out, and_11_out, and_12_out, and_13_out, and_14_out);
  or or_5 (w, not_36_out, and_15_out, and_16_out);
  and and_25 (and_25_out, not_39_out, not_40_out, d);
  and and_26 (and_26_out, not_41_out, b, c, d);
  and and_27 (and_27_out, a, not_42_out, not_43_out);
  and and_28 (and_28_out, a, c, not_44_out);
  or or_6 (z, and_20_out, and_21_out, and_22_out, and_23_out, and_24_out);
  or or_7 (s, and_25_out, and_26_out, and_27_out, and_28_out);
endmodule

module \tudo_o_que_é_feio  (
  input  in_1,
  output x,
  output y,
  output z,
  output u,
  output v,
  output w,
  output s
);

  wire clock_1_out, j_k_ff_1_q, j_k_ff_1_qn, j_k_ff_2_q, j_k_ff_2_qn, j_k_ff_3_q, j_k_ff_3_qn, j_k_ff_4_q;

  Clock clock_1 (.out(clock_1_out));
  J_K_Flip_Flop j_k_ff_1 (
    .J(in_1), .clk(clock_1_out), .K(in_1), .Q(j_k_ff_1_q), .Qn(j_k_ff_1_qn), .en(in_1));  // open: preset, reset
  J_K_Flip_Flop j_k_ff_2 (
    .J(in_1), .clk(j_k_ff_1_qn), .K(in_1), .Q(j_k_ff_2_q), .Qn(j_k_ff_2_qn), .en(in_1));  // open: preset, reset
  J_K_Flip_Flop j_k_ff_3 (
    .J(in_1), .clk(j_k_ff_2_qn), .K(in_1), .Q(j_k_ff_3_q), .Qn(j_k_ff_3_qn), .en(in_1));  // open: preset, reset
  J_K_Flip_Flop j_k_ff_4 (.J(in_1), .clk(j_k_ff_3_qn), .K(in_1), .Q(j_k_ff_4_q), .en(in_1));  // open: Qn, preset, reset
  main main_1 (
    .a(j_k_ff_4_q), .b(j_k_ff_3_q), .c(j_k_ff_2_q), .d(j_k_ff_1_q), .x(x), .y(y), .z(z), .u(u), .v(v), .w(w),
    .s(s));
  _7_Segment_Display u_7_segment_display_1 (.g(s), .f(w), .a(x), .b(y), .e(v), .d(u), .c(z));  // open: dp
endmodule
