// Logisim project dodecaedro.circ as structural Verilog: 4 circuits, main circuit main
module main (
);

  wire and_1_out, clock_1_out, display2_1_rr, display2_1_s, display2_1_u, display2_1_v, display2_1_vv,
       display2_1_w, display2_1_x, display2_1_y, display2_1_z;
  wire [2:0] adder_1_out, random_2_out;
  wire [3:0] adder_2_out, bit_extender_1_out, multiplexer_1_out, random_1_out;

  Clock clock_1 (.out(clock_1_out));
  Random #(.width(4)) random_1 (.clk(clock_1_out), .out(random_1_out));  // open: next, clr
  Random #(.width(3)) random_2 (.clk(clock_1_out), .out(random_2_out));  // open: next, clr
  Adder #(.width(3)) adder_1 (.a(random_2_out), .b(3'b001), .out(adder_1_out));  // open: cin, cout
  and and_1 (and_1_out, random_1_out[2], random_1_out[3]);
  assign bit_extender_1_out = {{1{1'b0}}, adder_1_out};  // Bit_Extender bit_extender_1
  Adder #(.width(4)) adder_2 (.a(random_1_out), .b(4'b0001), .out(adder_2_out));  // open: cin, cout
  Multiplexer #(.width(4)) multiplexer_1 (
    .in0(adder_2_out), .in1(bit_extender_1_out), .out(multiplexer_1_out), .sel(and_1_out));  // open: en
  // Probe on adder_2_out
  display2 display2_1 (
    .a(multiplexer_1_out[3]), .b(multiplexer_1_out[2]), .c(multiplexer_1_out[1]), .d(multiplexer_1_out[0]),
    .x(display2_1_x), .y(display2_1_y), .z(display2_1_z), .u(display2_1_u), .v(display2_1_v),
    .w(display2_1_w), .s(display2_1_s), .rr(display2_1_rr), .vv(display2_1_vv));
  _7_Segment_Display u_7_segment_display_1 (.b(display2_1_rr), .c(display2_1_vv));  // open: g, f, a, e, d, dp
  _7_Segment_Display u_7_segment_display_2 (
    .g(display2_1_s), .f(display2_1_w), .a(display2_1_x), .b(display2_1_y), .e(display2_1_v),
    .d(display2_1_u), .c(display2_1_z));  // open: dp
endmodule

module display (
  input  a,
  input  b,
  input  c,
  input  d,
  output x,
  output x_2,
  output y,
  output y_2,
  output z,
  output u,
  output v,
  output w,
  output s
);

  wire and_1_out, and_2_out, and_3_out, and_4_out, and_5_out, and_6_out, and_7_out, and_8_out, and_9_out,
       and_10_out, and_11_out, and_12_out, and_13_out, and_14_out, and_15_out, and_16_out, not_1_out,
       not_2_out, not_3_out, not_4_out, not_5_out, not_6_out, not_7_out, not_8_out, not_9_out, not_10_out,
       not_11_out, not_12_out, not_13_out, not_14_out, not_15_out, not_16_out, not_17_out, not_18_out,
       not_19_out, not_20_out, not_21_out;

  not not_1 (not_1_out, b);
  and and_1 (and_1_out, not_1_out, not_2_out);
  not not_2 (not_2_out, d);
  and and_2 (and_2_out, b, d);
  not not_3 (not_3_out, b);
  not not_4 (not_4_out, c);
  and and_3 (and_3_out, not_4_out, not_5_out);
  not not_5 (not_5_out, d);
  and and_4 (and_4_out, c, d);
  not not_6 (not_6_out, c);
  or or_1 (z, not_6_out, d, b);
  not not_7 (not_7_out, b);
  and and_5 (and_5_out, not_7_out, not_8_out);
  not not_8 (not_8_out, d);
  not not_9 (not_9_out, b);
  and and_6 (and_6_out, not_9_out, c);
  and and_7 (and_7_out, c, not_10_out);
  not not_10 (not_10_out, d);
  and and_8 (and_8_out, b, not_11_out, d);
  not not_11 (not_11_out, c);
  not not_12 (not_12_out, b);
  and and_9 (and_9_out, not_12_out, not_13_out);
  not not_13 (not_13_out, d);
  and and_10 (and_10_out, c, not_14_out);
  not not_14 (not_14_out, d);
  not not_15 (not_15_out, c);
  and and_11 (and_11_out, not_15_out, not_16_out);
  not not_16 (not_16_out, d);
  and and_12 (and_12_out, b, not_17_out);
  not not_17 (not_17_out, c);
  and and_13 (and_13_out, b, not_18_out);
  not not_18 (not_18_out, d);
  not not_19 (not_19_out, b);
  and and_14 (and_14_out, not_19_out, c);
  and and_15 (and_15_out, b, not_20_out);
  not not_20 (not_20_out, c);
  and and_16 (and_16_out, b, not_21_out);
  not not_21 (not_21_out, d);
  or or_2 (x, and_1_out, c, and_2_out, a);
  or or_3 (y, not_3_out, and_3_out, and_4_out);
  or or_4 (u, and_5_out, and_6_out, and_7_out, and_8_out, a);
  or or_5 (v, and_9_out, and_10_out);
  or or_6 (w, and_11_out, and_12_out, and_13_out, a);
  or or_7 (s, and_14_out, and_15_out, and_16_out, a);
endmodule

module display2 (
  input  a,
  input  b,
  input  c,
  input  d,
  output x,
  output y,
  output z,
  output u,
  output v,
  output w,
  output s,
  output rr,
  output vv
);

  wire and_1_out, and_2_out, and_3_out, and_4_out, and_5_out, and_6_out, and_7_out, and_8_out, and_9_out,
       and_10_out, and_11_out, and_12_out, and_13_out, and_14_out, and_15_out, and_16_out, and_17_out,
       and_18_out, and_19_out, and_20_out, and_21_out, and_22_out, and_23_out, and_24_out, and_25_out,
       and_26_out, and_27_out, and_28_out, and_29_out, and_30_out, and_31_out, and_32_out, and_33_out,
       and_34_out, and_35_out, not_1_out, not_2_out, not_3_out, not_4_out, not_5_out, not_6_out, not_7_out,
       not_8_out, not_9_out, not_10_out, not_11_out, not_12_out, not_13_out, not_14_out, not_15_out,
       not_16_out, not_17_out, not_18_out, not_19_out, not_20_out, not_21_out, not_22_out, not_23_out,
       not_24_out, not_25_out, not_26_out, not_27_out, not_28_out, not_29_out, not_30_out, not_31_out,
       not_32_out, not_33_out, not_34_out, not_35_out, not_36_out, not_37_out, not_38_out, not_39_out,
       not_40_out, not_41_out, not_42_out, not_43_out;

  not not_1 (not_1_out, b);
  and and_1 (and_1_out, not_1_out, not_2_out);
  not not_2 (not_2_out, d);
  not not_3 (not_3_out, a);
  and and_2 (and_2_out, not_3_out, c);
  and and_3 (and_3_out, b, d);
  and and_4 (and_4_out, a, not_4_out);
  not not_4 (not_4_out, c);
  not not_5 (not_5_out, b);
  not not_6 (not_6_out, c);
  and and_5 (and_5_out, not_6_out, not_7_out);
  not not_7 (not_7_out, d);
  not not_8 (not_8_out, a);
  and and_6 (and_6_out, not_8_out, c, d);
  and and_7 (and_7_out, a, not_9_out);
  not not_9 (not_9_out, c);
  and and_8 (and_8_out, a, not_10_out);
  not not_10 (not_10_out, d);
  not not_11 (not_11_out, a);
  and and_9 (and_9_out, not_11_out, not_12_out);
  not not_12 (not_12_out, c);
  and and_10 (and_10_out, b, c);
  and and_11 (and_11_out, a, not_13_out);
  not not_13 (not_13_out, b);
  not not_14 (not_14_out, b);
  and and_12 (and_12_out, not_14_out, not_15_out);
  not not_15 (not_15_out, d);
  not not_16 (not_16_out, a);
  not not_17 (not_17_out, b);
  and and_13 (and_13_out, not_16_out, not_17_out, c);
  not not_18 (not_18_out, a);
  and and_14 (and_14_out, not_18_out, c, not_19_out);
  not not_19 (not_19_out, d);
  not not_20 (not_20_out, c);
  and and_15 (and_15_out, b, not_20_out, d);
  and and_16 (and_16_out, a, not_21_out);
  not not_21 (not_21_out, c);
  and and_17 (and_17_out, a, b, d);
  not not_22 (not_22_out, b);
  and and_18 (and_18_out, not_22_out, not_23_out);
  not not_23 (not_23_out, d);
  not not_24 (not_24_out, a);
  and and_19 (and_19_out, not_24_out, c, not_25_out);
  not not_25 (not_25_out, d);
  not not_26 (not_26_out, c);
  and and_20 (and_20_out, a, not_26_out, not_27_out);
  not not_27 (not_27_out, d);
  not not_28 (not_28_out, a);
  and and_21 (and_21_out, not_28_out, not_29_out, not_30_out);
  not not_29 (not_29_out, c);
  not not_30 (not_30_out, d);
  not not_31 (not_31_out, a);
  and and_22 (and_22_out, not_31_out, b, not_32_out);
  not not_32 (not_32_out, c);
  not not_33 (not_33_out, a);
  and and_23 (and_23_out, not_33_out, b, not_34_out);
  not not_34 (not_34_out, d);
  and and_24 (and_24_out, a, not_35_out, not_36_out);
  not not_35 (not_35_out, b);
  not not_36 (not_36_out, c);
  not not_37 (not_37_out, b);
  and and_25 (and_25_out, a, not_37_out, not_38_out);
  not not_38 (not_38_out, d);
  and and_26 (and_26_out, a, b, c);
  not not_39 (not_39_out, a);
  not not_40 (not_40_out, b);
  and and_27 (and_27_out, not_39_out, not_40_out, c);
  and and_28 (and_28_out, b, not_41_out);
  not not_41 (not_41_out, c);
  and and_29 (and_29_out, b, not_42_out);
  not not_42 (not_42_out, d);
  and and_30 (and_30_out, a, not_43_out);
  not not_43 (not_43_out, c);
  and and_31 (and_31_out, a, b);
  and and_32 (and_32_out, a, c);
  and and_33 (and_33_out, a, b);
  and and_34 (and_34_out, a, c);
  and and_35 (and_35_out, a, b);
  or or_1 (x, and_1_out, and_2_out, and_3_out, and_4_out);
  or or_2 (y, not_5_out, and_5_out, and_6_out, and_7_out, and_8_out);
  or or_3 (z, and_9_out, d, and_10_out, and_11_out);
  or or_4 (v, and_18_out, and_19_out, and_20_out);
  or or_5 (s, and_27_out, and_28_out, and_29_out, and_30_out, and_31_out);
  or or_6 (rr, and_32_out, and_33_out);
  or or_7 (vv, and_34_out, and_35_out);
  or or_8 (u, and_12_out, and_13_out, and_14_out, and_15_out, and_16_out, and_17_out);
  or or_9 (w, and_21_out, and_22_out, and_23_out, and_24_out, and_25_out, and_26_out);
endmodule

module original (
);

  main main_1 ();
endmodule
